// Logisim project blank_simple_cpu.circ as structural Verilog: 11 circuits, main circuit main
module main (
);

  wire alu_1_correct, alucontrolunit_1_correct, controlunit_1_correct, instmemory_1_correct, pc_1_correct,
       registerfile_1_correct, regwritecontrol_1_wen;

  LED led_1 (.in(pc_1_correct));
  PC pc_1 (.Correct(pc_1_correct));  // open: data, pc
  Adder #(.width(32)) adder_1 (.a(32'h4));  // open: b, out, cin, cout
  LED led_2 (.in(instmemory_1_correct));
  InstMemory instmemory_1 (.Correct(instmemory_1_correct));  // open: address, instruction
  RegWriteControl regwritecontrol_1 (.wen(regwritecontrol_1_wen));  // open: writereg
  LED led_3 (.in(controlunit_1_correct));
  LED led_4 (.in(registerfile_1_correct));
  ControlUnit controlunit_1 (.Correct(controlunit_1_correct));  // open: opcode, branch, itype, memop, aluop, xsrc, ysrc, toreg, writereg, plus4, jal, jalr, resultselect, validinst
  ImmediateGenerator immediategenerator_1 ();  // open: instruction, sextImm
  RegisterFile registerfile_1 (
    .wen(regwritecontrol_1_wen), .Correct(registerfile_1_correct));  // open: readreg1, readreg2, writereg, writedata, readdata1, readdata2
  LED led_5 (.in(alucontrolunit_1_correct));
  LED led_6 (.in(alu_1_correct));
  NextPCUnit nextpcunit_1 ();  // open: branch, jal, jalr, eqf, ltf, funct3, pc, imm, nextpc, taken
  ALUControlUnit alucontrolunit_1 (.Correct(alucontrolunit_1_correct));  // open: itype, aluop, funct7, funct3, result
  ALU alu_1 (.Correct(alu_1_correct));  // open: operation, inputx, inputy, result, eqf, ltf
  DataMemory datamemory_1 ();  // open: address, writedata, memread, memwrite, maskmode, readdata, valid, sext

  // Notes on the sheet:
  //   pcPlusFour
endmodule

module PC (
  input  [31:0] data,
  output Correct,
  output [31:0] pc
);

  Comparator #(.width(32), .mode("unsigned")) comparator_1 (.a(data), .b(32'h8), .eq(Correct));  // open: gt, lt

  assign pc = 32'h4;
endmodule

module InstMemory (
  input  [31:0] address,
  output Correct,
  output [31:0] instruction
);

  Comparator #(.width(32), .mode("unsigned")) comparator_1 (.a(address), .b(32'h4), .eq(Correct));  // open: gt, lt

  assign instruction = 32'h4945501;
endmodule

module ImmediateGenerator (
  input  [31:0] instruction,
  output [31:0] sextImm
);

  wire comparator_1_eq;

  Comparator #(.width(32), .mode("unsigned")) comparator_1 (
    .a(instruction), .b(32'h4945501), .eq(comparator_1_eq));  // open: gt, lt

  assign sextImm = 32'h2;
endmodule

module RegisterFile (
  input  [4:0] readreg1,
  input  [4:0] readreg2,
  input  [4:0] writereg,
  input  wen,
  input  [31:0] writedata,
  output Correct,
  output [31:0] readdata1,
  output [31:0] readdata2
);

  wire comparator_1_eq, comparator_2_eq, comparator_3_eq, comparator_4_eq;

  Comparator #(.width(5), .mode("unsigned")) comparator_1 (
    .a(readreg1), .b(5'b01000), .eq(comparator_1_eq));  // open: gt, lt
  Comparator #(.width(5), .mode("unsigned")) comparator_2 (
    .a(readreg2), .b(5'b01001), .eq(comparator_2_eq));  // open: gt, lt
  Comparator #(.width(5), .mode("unsigned")) comparator_3 (
    .a(writereg), .b(5'b01010), .eq(comparator_3_eq));  // open: gt, lt
  Comparator #(.width(32), .mode("unsigned")) comparator_4 (
    .a(writedata), .b(32'ha5a5ff00), .eq(comparator_4_eq));  // open: gt, lt
  and and_1 (Correct, comparator_1_eq, comparator_2_eq, comparator_3_eq, wen, comparator_4_eq);

  assign readdata1 = 32'h72656731;
  assign readdata2 = 32'h72656732;
endmodule

module ALU (
  input  [3:0] operation,
  input  [31:0] inputx,
  input  [31:0] inputy,
  output Correct,
  output [31:0] result,
  output eqf,
  output ltf
);

  wire comparator_1_eq, comparator_2_eq, comparator_3_eq;

  Comparator #(.width(4), .mode("unsigned")) comparator_1 (
    .a(operation), .b(4'b1101), .eq(comparator_1_eq));  // open: gt, lt
  Comparator #(.width(32), .mode("unsigned")) comparator_2 (
    .a(inputx), .b(32'h72656731), .eq(comparator_2_eq));  // open: gt, lt
  Comparator #(.width(32), .mode("unsigned")) comparator_3 (
    .a(inputy), .b(32'h72656732), .eq(comparator_3_eq));  // open: gt, lt
  and and_1 (Correct, comparator_1_eq, comparator_2_eq, comparator_3_eq);

  assign eqf = 1'b0;
  assign ltf = 1'b0;
  assign result = 32'ha5a5ff00;
endmodule

module ALUControlUnit (
  input  itype,
  input  aluop,
  input  [2:0] funct3,
  input  [6:0] funct7,
  output Correct,
  output [3:0] result
);

  wire comparator_1_eq, comparator_2_eq, not_1_out;

  not not_1 (not_1_out, itype);
  Comparator #(.width(3), .mode("unsigned")) comparator_1 (
    .a(funct3), .b(3'b101), .eq(comparator_1_eq));  // open: gt, lt
  Comparator #(.width(7), .mode("unsigned")) comparator_2 (
    .a(funct7), .b(7'b0000010), .eq(comparator_2_eq));  // open: gt, lt
  and and_1 (Correct, not_1_out, aluop, comparator_1_eq, comparator_2_eq);

  assign result = 4'b1101;
endmodule

module ControlUnit (
  input  [6:0] opcode,
  output Correct,
  output branch,
  output jal,
  output jalr,
  output itype,
  output aluop,
  output xsrc,
  output ysrc,
  output plus4,
  output resultselect,
  output [1:0] memop,
  output toreg,
  output writereg,
  output validinst
);

  Comparator #(.width(7), .mode("unsigned")) comparator_1 (.a(opcode), .b(7'b0000001), .eq(Correct));  // open: gt, lt

  assign aluop = 1'b1;
  assign branch = 1'b1;
  assign itype = 1'b1;
  assign jal = 1'b1;
  assign jalr = 1'b1;
  assign memop = 2'b11;
  assign plus4 = 1'b1;
  assign resultselect = 1'b1;
  assign toreg = 1'b1;
  assign validinst = 1'b1;
  assign writereg = 1'b1;
  assign xsrc = 1'b1;
  assign ysrc = 1'b1;
endmodule

module DataMemory (
  input  [31:0] address,
  input  memread,
  input  memwrite,
  input  valid,
  input  [1:0] maskmode,
  input  sext,
  input  [31:0] writedata,
  output [31:0] readdata
);
endmodule

module NextPCUnit (
  input  branch,
  input  jal,
  input  jalr,
  input  eqf,
  input  ltf,
  input  [2:0] funct3,
  input  [31:0] pc,
  input  [31:0] imm,
  output [31:0] nextpc,
  output taken
);
endmodule

module RegWriteControl (
  input  [4:0] writereg,
  output wen
);

  Comparator #(.width(5)) comparator_1 (.a(writereg), .b(5'b01010), .eq(wen));  // open: gt, lt
endmodule
